// Digital circuit RAM.dig as structural Verilog
module RAM (
  input  [15:0] TEST_DATA,
  input  TEST_SEND,
  input  clk
);

  wire and_1_out, and_2_out, and_4_out, and_5_out, and_6_out, and_7_out, and_8_out, and_9_out, and_10_out,
       and_11_out, and_12_out, and_13_out, and_14_out, and_15_out, and_16_out, bus_debugger_1_fb,
       delay_1_out, delay_2_out, delay_3_out, initial_q, or_1_out, or_2_out, or_3_out, or_5_out, or_6_out,
       or_7_out, or_8_out, reading1_q, reading2_nq, reading2_q, RST, writing1_q, writing2_nq, writing2_q,
       writing3_nq;
  wire [2:0] ADDR_BUFFER_q, and_3_out, bus_debugger_1_last_addr_out;
  wire [2:2] writing3_q;
  wire [3:0] pulldown_1_out;
  wire [7:0] driver_1_out, driver_1_out_2, WRITE_BUFFER_q;
  wire [8:0] driver_3_out;
  wire [9:0] d_ff_1_q;
  wire [15:0] bus_debugger_1_last_data_out, driver_2_out, pulldown_2_out;
  wire [15:13] driver_3_out_2;

  PullDown pulldown_1 (.out(pulldown_1_out[0]));
  assign {driver_1_out_2, driver_1_out} = and_1_out ? driver_2_out : 16'bz;  // Driver driver_1
  assign driver_2_out = or_7_out ? pulldown_2_out : 16'bz;  // Driver driver_2
  assign {driver_3_out_2, driver_3_out, pulldown_1_out} = and_2_out ? driver_2_out : 16'bz;  // Driver driver_3
  Reset_On_First_Clock reset_on_first_clock_1 (.CLK(clk), .RST(RST));
  and and_1 (and_1_out, writing1_q, ~or_7_out);  // And
  and and_2 (and_2_out, ~or_7_out, ~writing1_q);  // And
  // Probe CLK on clk
  D_FF #(.Bits(8)) READ_BUFFER (.D(pulldown_2_out[15:8]), .C(delay_1_out), .Q(pulldown_2_out[7:0]));  // open: nQ
  assign and_3_out = ~{3{writing3_q[2]}} & ADDR_BUFFER_q;  // And and_3, 3 bits wide
  PullDown #(.Bits(8)) pulldown_2 (.out(pulldown_2_out[15:8]));
  Bus_Debugger bus_debugger_1 (
    .DATA(driver_2_out), .ADDR(and_3_out), .TB(and_4_out), .TEST_DATA(TEST_DATA), .TEST_SEND(TEST_SEND),
    .FB(bus_debugger_1_fb), .LAST_DATA_OUT(bus_debugger_1_last_data_out),
    .LAST_ADDR_OUT(bus_debugger_1_last_addr_out));
  and and_4 (and_4_out, ~clk, or_7_out);  // And
  D_FF #(.Bits(3)) ADDR_BUFFER (.D(driver_3_out_2), .C(and_5_out), .Q(ADDR_BUFFER_q));  // open: nQ
  and and_5 (and_5_out, clk, and_7_out);
  Delay delay_1 (.in(delay_3_out), .out(delay_1_out));
  Delay delay_2 (.in(reading1_q), .out(delay_2_out));
  Delay delay_3 (.in(delay_2_out), .out(delay_3_out));
  and and_6 (and_6_out, bus_debugger_1_fb, clk);
  assign pulldown_2_out[15:8] = or_1_out ? WRITE_BUFFER_q : 8'bz;  // Driver driver_4
  assign pulldown_2_out[15:8] = writing1_q ? driver_1_out : 8'bz;  // Driver driver_5
  LED led_1 (.in(bus_debugger_1_last_data_out[1]));
  LED led_2 (.in(bus_debugger_1_last_data_out[3]));
  LED led_3 (.in(bus_debugger_1_last_data_out[0]));
  LED led_4 (.in(bus_debugger_1_last_data_out[2]));
  and and_7 (and_7_out, ~writing1_q, bus_debugger_1_fb);  // And
  D_FF #(.Bits(8)) WRITE_BUFFER (.D(driver_1_out_2), .C(and_6_out), .Q(WRITE_BUFFER_q));  // open: nQ
  LED led_5 (.in(bus_debugger_1_last_data_out[5]));
  LED led_6 (.in(bus_debugger_1_last_data_out[7]));
  LED led_7 (.in(bus_debugger_1_last_data_out[4]));
  LED led_8 (.in(bus_debugger_1_last_data_out[6]));
  or or_1 (or_1_out, writing2_q, writing3_q[2]);
  LED led_9 (.in(bus_debugger_1_last_data_out[9]));
  LED led_10 (.in(bus_debugger_1_last_data_out[11]));
  LED led_11 (.in(bus_debugger_1_last_data_out[8]));
  LED led_12 (.in(bus_debugger_1_last_data_out[10]));
  RAMSinglePortSel #(.AddrBits(10), .Bits(8)) ramsingleportsel_1 (
    .A(d_ff_1_q), .CS(1'b1), .WE(or_2_out), .OE(~or_2_out), .D(pulldown_2_out[15:8]));
  LED led_13 (.in(bus_debugger_1_last_data_out[13]));
  LED led_14 (.in(bus_debugger_1_last_data_out[15]));
  LED led_15 (.in(bus_debugger_1_last_data_out[12]));
  LED led_16 (.in(bus_debugger_1_last_data_out[14]));
  LED led_17 (.in(bus_debugger_1_last_addr_out[1]));
  LED led_18 (.in(bus_debugger_1_last_addr_out[0]));
  or or_2 (or_2_out, writing2_q, writing3_q[2], writing1_q);
  LED led_19 (.in(bus_debugger_1_last_addr_out[2]));
  or or_3 (or_3_out, reading1_q, RST, and_7_out);
  or or_4 (d_ff_1_q[9], reading2_q, writing2_q);
  or or_5 (or_5_out, or_7_out, RST, and_7_out);
  D_FF #(.Bits(9)) d_ff_1 (.D(driver_3_out), .C(and_12_out), .Q(d_ff_1_q[8:0]));  // open: nQ
  or or_6 (or_6_out, or_7_out, RST);
  and and_8 (and_8_out, or_5_out, clk);
  and and_9 (and_9_out, initial_q, ~RST, ~pulldown_1_out[0]);  // And
  and and_10 (and_10_out, or_3_out, clk);
  and and_11 (and_11_out, reading2_nq, reading1_q);
  or or_7 (or_7_out, writing3_q[2], reading2_q);
  and and_12 (and_12_out, clk, and_7_out);
  D_FF \initial  (.D(or_6_out), .C(and_8_out), .Q(initial_q));  // open: nQ
  D_FF reading1 (.D(and_9_out), .C(and_10_out), .Q(reading1_q));  // open: nQ
  D_FF reading2 (.D(and_11_out), .C(clk), .Q(reading2_q), .nQ(reading2_nq));
  or or_8 (or_8_out, RST, bus_debugger_1_fb);
  and and_13 (and_13_out, writing2_nq, bus_debugger_1_fb, writing1_q);
  and and_14 (and_14_out, initial_q, ~RST, pulldown_1_out[0]);  // And
  and and_15 (and_15_out, clk, or_8_out);
  and and_16 (and_16_out, writing3_nq, writing2_q);
  D_FF writing1 (.D(and_14_out), .C(and_15_out), .Q(writing1_q));  // open: nQ
  D_FF writing2 (.D(and_13_out), .C(clk), .Q(writing2_q), .nQ(writing2_nq));
  D_FF writing3 (.D(and_16_out), .C(clk), .Q(writing3_q[2]), .nQ(writing3_nq));

  // Notes on the sheet:
  //   FB cutoff
  //   on write
  //   WE
  //   HIGH-ADDR
  //   TB
  //   STATE REGISTERS
endmodule
